# Fritzing sketch schematic (saved by Fritzing 0.9.2b)
breadboards: 1

parts:
  Part1 = Arduino Uno (Rev3)
  R1 = Resistor [tolerance=±5% resistance=330 package=THT]
  R2 = Resistor [tolerance=±5% resistance=330 package=THT]
  R3 = Resistor [tolerance=±5% resistance=330 package=THT]
  LED1 = LED - 3mm [color="Red (633nm)" package="3 mm [THT]"]
  LED3 = LED - 3mm [color="Green (570nm)" package="3 mm [THT]"]
  LED2 = LED - 3mm [color="Yellow (595nm)" package="3 mm [THT]"]
  J1 = Piezo Speaker

nets:
  N1: Part1.D8, R1.Pin_0
  N2: Part1.D9_PWM, R2.Pin_0
  N3: Part1.D10_PWM/SS, R3.Pin_0
  GND: Part1.GND, LED1.cathode, LED3.cathode, LED2.cathode, J1.pin1
  N4: Part1.D6_PWM, J1.pin2
  N5: R1.Pin_1, LED1.anode
  N6: R2.Pin_1, LED2.anode
  N7: R3.Pin_1, LED3.anode
